// Logisim project assignment1.circ as structural Verilog: 1 circuit, main circuit main
module main (
  input  [3:0] Bo,
  input  [3:0] A1,
  input  Cin,
  input  S1,
  input  S0,
  input  Con,
  input  Con_2,
  input  Con_3,
  output [3:0] D3,
  output Cout,
  output [3:0] D3_2,
  output [3:0] D3_3,
  output [3:0] D3_4
);

  wire adder_1_cout, adder_2_cout, adder_3_cout, and_1_out, and_2_out, and_3_out, and_4_out,
       multiplexer_1_out, multiplexer_2_out, multiplexer_3_out, multiplexer_4_out, not_1_out, not_2_out,
       not_3_out, not_4_out, not_5_out, not_6_out, not_7_out, not_8_out, or_1_out, or_2_out, or_3_out,
       or_4_out, xor_1_out, xor_2_out, xor_3_out, xor_4_out;

  not not_1 (not_1_out, Bo[3]);
  not not_2 (not_2_out, Bo[2]);
  not not_3 (not_3_out, Bo[1]);
  not not_4 (not_4_out, Bo[0]);
  not not_5 (not_5_out, A1[0]);
  not not_6 (not_6_out, A1[1]);
  not not_7 (not_7_out, A1[2]);
  and and_1 (and_1_out, A1[0], Bo[3]);
  or or_1 (or_1_out, A1[0], Bo[3]);
  xor xor_1 (xor_1_out, A1[0], Bo[3]);
  and and_2 (and_2_out, A1[1], Bo[2]);
  or or_2 (or_2_out, A1[1], Bo[2]);
  xor xor_2 (xor_2_out, A1[1], Bo[2]);
  and and_3 (and_3_out, A1[2], Bo[1]);
  or or_3 (or_3_out, A1[2], Bo[1]);
  xor xor_3 (xor_3_out, A1[2], Bo[1]);
  and and_4 (and_4_out, A1[3], Bo[0]);
  or or_4 (or_4_out, A1[3], Bo[0]);
  xor xor_4 (xor_4_out, A1[3], Bo[0]);
  not not_8 (not_8_out, A1[3]);
  Multiplexer #(.select(2)) multiplexer_1 (
    .in0(1'b0), .in1(Bo[3]), .in2(not_1_out), .in3(1'b1), .out(multiplexer_1_out), .sel({S1, S0}));  // open: en
  Multiplexer #(.select(2)) multiplexer_2 (
    .in0(1'b0), .in1(Bo[2]), .in2(not_2_out), .in3(1'b1), .out(multiplexer_2_out), .sel({S1, S0}));  // open: en
  Multiplexer #(.select(2)) multiplexer_3 (
    .in0(1'b0), .in1(Bo[1]), .in2(not_3_out), .in3(1'b1), .out(multiplexer_3_out), .sel({S1, S0}));  // open: en
  Multiplexer #(.select(2)) multiplexer_4 (
    .in0(1'b0), .in1(Bo[0]), .in2(not_4_out), .in3(1'b1), .out(multiplexer_4_out), .sel({S1, S0}));  // open: en
  Adder #(.width(1)) adder_1 (.a(A1[0]), .b(multiplexer_1_out), .out(D3[0]), .cin(Cin), .cout(adder_1_cout));
  Adder #(.width(1)) adder_2 (.a(A1[1]), .b(multiplexer_2_out), .out(D3[1]), .cin(adder_1_cout), .cout(adder_2_cout));
  Adder #(.width(1)) adder_3 (.a(A1[2]), .b(multiplexer_3_out), .out(D3[2]), .cin(adder_2_cout), .cout(adder_3_cout));
  Adder #(.width(1)) adder_4 (.a(A1[3]), .b(multiplexer_4_out), .out(D3[3]), .cin(adder_3_cout), .cout(Cout));
  Multiplexer #(.select(2)) multiplexer_5 (
    .in0(and_1_out), .in1(or_1_out), .in2(xor_1_out), .in3(not_5_out), .out(D3_2[0]), .sel({S1, S0}));  // open: en
  Multiplexer #(.select(2)) multiplexer_6 (
    .in0(and_2_out), .in1(or_2_out), .in2(xor_2_out), .in3(not_6_out), .out(D3_2[1]), .sel({S1, S0}));  // open: en
  Multiplexer #(.select(2)) multiplexer_7 (
    .in0(and_3_out), .in1(or_3_out), .in2(xor_3_out), .in3(not_7_out), .out(D3_2[2]), .sel({S1, S0}));  // open: en
  Multiplexer #(.select(2)) multiplexer_8 (
    .in0(and_4_out), .in1(or_4_out), .in2(xor_4_out), .in3(not_8_out), .out(D3_2[3]), .sel({S1, S0}));  // open: en
  Multiplexer #(.select(2)) multiplexer_9 (
    .in0(Con), .in1(A1[1]), .in2(A1[3]), .in3(A1[1]), .out(D3_3[0]), .sel({S1, S0}), .en(1'b1));
  Multiplexer #(.select(2)) multiplexer_10 (
    .in0(A1[0]), .in1(A1[2]), .in2(A1[0]), .in3(A1[2]), .out(D3_3[1]), .sel({S1, S0}), .en(1'b1));
  Multiplexer #(.select(2)) multiplexer_11 (
    .in0(A1[1]), .in1(A1[3]), .in2(A1[1]), .in3(A1[3]), .out(D3_3[2]), .sel({S1, S0}), .en(1'b1));
  Multiplexer #(.select(2)) multiplexer_12 (
    .in0(A1[2]), .in1(Con_2), .in2(A1[2]), .in3(A1[0]), .out(D3_3[3]), .sel({S1, S0}), .en(1'b1));
  Multiplexer multiplexer_13 (.in0(A1[1]), .in1(Con_3), .out(D3_4[0]), .sel(S0), .en(1'b1));
  Multiplexer multiplexer_14 (.in0(A1[2]), .in1(A1[0]), .out(D3_4[1]), .sel(S0), .en(1'b1));
  Multiplexer multiplexer_15 (.in0(A1[3]), .in1(A1[1]), .out(D3_4[2]), .sel(S0), .en(1'b1));
  Multiplexer multiplexer_16 (.in0(A1[3]), .in1(A1[2]), .out(D3_4[3]), .sel(S0), .en(1'b1));

  // Notes on the sheet:
  //   B1
  //   B3
  //   B2
  //   Ao
  //   A3
  //   A2
  //   0
  //   1
  //   AND
  //   OR
  //   XOR
  //   NOT
  //   D2
  //   D1
  //   Do
  //   Arithmetic Unit
  //   Logic Unit
  //   D2
  //   D1
  //   Do
  //   Shift Unit
  //   (shl/shr/cil/cir)
  //   D2
  //   18BCE248
  //   D1
  //   Do
  //   ALS Unit
  //   Arithmetic Shift Unit
  //   D2
  //   D1
  //   Do
endmodule
